# Fritzing sketch circuit diagram (saved by Fritzing 0.9.5d)

parts:
  Part1 = Arduino Nano (Rev3.0)
  J1 = Piezo Speaker
  Part2 = Bluetooth HC-05 Macho

nets:
  GND: Part1.GND, J1.pin1, Part2.GND
  N1: Part1.D8, J1.pin2
  N2: Part1.D10, Part2.TXD
  N3: Part1.D11/MOSI, Part2.RXD
  5V: Part1.5V, Part2.VCC
